# Fritzing sketch circuit_ver2.0 (saved by Fritzing 0.9.0b)
breadboards: 1

parts:
  パーツ1 = Arduino Uno (Rev3)
  VCC1 = Battery block 9V
  U1 = TA7291P [package=HSIP10-P-2.54(THT)]
  U2 = TA7291P [package=HSIP10-P-2.54(THT)]
  U3 = TA7291P [package=HSIP10-P-2.54(THT)]
  M1 = DC Motor
  M2 = DC Motor
  M3 = DC Motor
  VCC2 = 4 x AAA Battery Mount

nets:
  N1: パーツ1.D9_PWM, U1.IN1
  N2: パーツ1.D10_PWM/SS, U3.Vref
  N3: パーツ1.D11_PWM/MOSI, U1.IN2
  N4: パーツ1.D12/MISO, U3.IN1
  N5: パーツ1.D13/SCK, U3.IN2
  N6: パーツ1.D2, U2.IN1
  N7: パーツ1.D3_PWM, U2.Vref
  N8: パーツ1.D5_PWM, U2.IN2
  N9: パーツ1.D6_PWM, U1.Vref
  VCC: パーツ1.5V, U1.Vcc, U2.Vcc, U3.Vcc
  GND: パーツ1.GND, VCC1.-, U1.GND, U2.GND, U3.GND, VCC2.-
  N10: パーツ1.VIN, VCC1.+
  N11: U1.OUT1, M1.pin_2
  N12: U1.Vs, U2.Vs, U3.Vs, VCC2.+
  N13: U1.OUT2, M1.pin_1
  N14: U2.OUT1, M2.pin_2
  N15: U2.OUT2, M2.pin_1
  N16: U3.OUT1, M3.pin_2
  N17: U3.OUT2, M3.pin_1

notes:
  right motor
  left motor
  under motor
  R2006GS(受信機)
  3ch
  2ch
  4ch

custom parts:
  TA7291P: The IC are Full-Bridge Driver. 4 modes available (CW / CCW / STOP / BRAKE) and PWM control. Output current:1.0 A (AVE.) 2.0 A (PEAK)
